// Logisim project triggers.circ as structural Verilog: 1 circuit, main circuit main
module main (
  input  in_1,
  input  in_2,
  output out_3
);

  wire or_1_out;

  or or_1 (or_1_out, out_3, in_1);
  and and_1 (out_3, or_1_out, ~in_2);  // AND_Gate
endmodule
