// Logisim project triggers.circ as structural Verilog: 1 circuit, main circuit main
module main (
  input  in_1,
  input  in_2,
  input  in_3,
  input  in_4,
  input  in_5,
  output out_6,
  output out_7,
  output out_8
);

  wire and_1_out, and_2_out, not_1_out, not_2_out, or_1_out, or_2_out, or_3_out;

  not not_1 (not_1_out, in_3);
  not not_2 (not_2_out, in_4);
  or or_1 (or_1_out, out_6, in_1);
  and and_1 (and_1_out, in_4, in_5);
  and and_2 (and_2_out, in_5, not_2_out);
  and and_3 (out_6, or_1_out, ~in_2);  // AND_Gate
  or or_2 (or_2_out, out_7, in_3);
  or or_3 (or_3_out, out_8, and_1_out);
  and and_4 (out_7, or_2_out, ~not_1_out);  // AND_Gate
  and and_5 (out_8, or_3_out, ~and_2_out);  // AND_Gate
endmodule
